# Fritzing sketch Conexiones Maquina Fundas (saved by Fritzing 0.9.3b)

parts:
  Componente1 = Arduino Uno (Rev3)
  S1 = Momentary Switch [package=ksa_sealed_tac_switch]
  J1 = Basic Servo
  R1 = Resistor [tolerance=±5% resistance=220 package="2512 [SMD]"]

nets:
  N1: Componente1.D2, S1.1
  N2: Componente1.D3_PWM, J1.pulse
  N3: Componente1.5V, S1.4
  GND: Componente1.GND, J1.gnd, R1.Pin_0
  N4: S1.2, R1.Pin_1
  N5: S1.3, J1.vcc
